// Logisim project CPU.circ as structural Verilog: 2 circuits, main circuit ULA
module ULA (
  input  [15:0] A,
  input  [15:0] B,
  input  [3:0] op
);

  Adder #(.width(16)) adder_1 (.a(A), .b(B));  // open: out, cin, cout
endmodule

module Soma (
  input  in_1,
  input  in_2,
  output out_3,
  output out_4
);

  xor xor_1 (out_3, in_1, in_2);
  and and_1 (out_4, in_1, in_2);
endmodule
